// Logisim project branch-comp.circ as structural Verilog: 1 circuit, main circuit branch_comp
module branch_comp (
  input  [31:0] BrData1,
  input  [31:0] BrData2,
  input  BrUn,
  output BrEq,
  output BrLt
);

  wire not_1_out;
  wire [31:0] controlled_buffer_1_out, controlled_buffer_2_out, controlled_buffer_3_out,
       controlled_buffer_4_out;

  not not_1 (not_1_out, BrUn);
  assign controlled_buffer_1_out = BrUn ? BrData1 : 32'bz;  // Controlled_Buffer controlled_buffer_1
  assign controlled_buffer_2_out = BrUn ? BrData2 : 32'bz;  // Controlled_Buffer controlled_buffer_2
  assign controlled_buffer_3_out = not_1_out ? BrData1 : 32'bz;  // Controlled_Buffer controlled_buffer_3
  assign controlled_buffer_4_out = not_1_out ? BrData2 : 32'bz;  // Controlled_Buffer controlled_buffer_4
  Comparator #(.mode("unsigned"), .width(32)) comparator_1 (
    .a(controlled_buffer_1_out), .b(controlled_buffer_2_out), .eq(BrEq), .lt(BrLt));  // open: gt
  Comparator #(.width(32)) comparator_2 (
    .a(controlled_buffer_3_out), .b(controlled_buffer_4_out), .eq(BrEq), .lt(BrLt));  // open: gt

  // Notes on the sheet:
  //   INPUTS to your circuit
  //   Unsigned
  //   2-complements/Signed
  //   DON'T CHANGE THE LOCATIONS OF THE INPUTS AND OUTPUTS!
  //   OUTPUT from your circuit
endmodule
