// Logisim project control-logic.circ as structural Verilog: 1 circuit, main circuit control_logic
module control_logic (
  input  [31:0] Instruction,
  input  BrEq,
  input  BrLt,
  output PCSel,
  output RegWEn,
  output [2:0] ImmSel,
  output BrUn,
  output ASel,
  output BSel,
  output [3:0] ALUSel,
  output MemWEn,
  output [1:0] WBSel
);

  wire comparator_1_eq, comparator_5_eq, comparator_8_eq, comparator_9_eq, controlled_buffer_12_out, d1_0,
       d1_1, d1_5, d2_5, is_add, is_addi, is_and, is_andi, is_auipc, is_beq, is_bge, is_bgeu, is_blt,
       is_bltu, is_bne, is_branch, is_jal, is_jalr, is_lb, is_lh, is_lui, is_lw, is_mul, is_mulh, is_mulhu,
       is_or, is_ori, is_sb, is_sh, is_sll, is_slli, is_slt, is_slti, is_sra, is_srai, is_srl, is_srli,
       is_sub, is_sw, is_xor, is_xori, not_1_out, not_2_out, or_1_out, or_2_out, or_3_out;
  wire [2:0] controlled_buffer_5_out, controlled_buffer_6_out, controlled_buffer_7_out,
       controlled_buffer_8_out, controlled_buffer_9_out;
  wire [5:0] ROMInput;
  wire [6:0] controlled_buffer_1_out, controlled_buffer_2_out, controlled_buffer_3_out,
       controlled_buffer_4_out;
  wire [15:14] rom_1_data;

  Comparator #(.width(7)) comparator_1 (.a(Instruction[6:0]), .b(7'b0110011), .eq(comparator_1_eq));  // open: gt, lt
  assign controlled_buffer_1_out = d1_0 ? Instruction[31:25] : 7'bz;  // Controlled_Buffer controlled_buffer_1
  Comparator #(.width(7)) comparator_2 (
    .a(controlled_buffer_1_out), .b(7'b0000001), .gt(is_sub), .eq(is_mul), .lt(is_add));
  assign controlled_buffer_2_out = d1_1 ? Instruction[31:25] : 7'bz;  // Controlled_Buffer controlled_buffer_2
  Comparator #(.width(7)) comparator_3 (
    .a(controlled_buffer_2_out), .b(7'b0000001), .eq(is_mulh), .lt(is_sll));  // open: gt
  assign controlled_buffer_3_out = d1_5 ? Instruction[31:25] : 7'bz;  // Controlled_Buffer controlled_buffer_3
  Comparator #(.width(7)) comparator_4 (
    .a(controlled_buffer_3_out), .b({7{1'b0}}), .gt(is_sra), .eq(is_srl));  // open: lt
  Comparator #(.width(7)) comparator_5 (.a(Instruction[6:0]), .b(7'b0010011), .eq(comparator_5_eq));  // open: gt, lt
  assign controlled_buffer_4_out = d2_5 ? Instruction[31:25] : 7'bz;  // Controlled_Buffer controlled_buffer_4
  assign controlled_buffer_5_out = comparator_1_eq ? Instruction[14:12] : 3'bz;  // Controlled_Buffer controlled_buffer_5
  Decoder #(.select(3)) decoder_1 (
    .out0(d1_0), .out1(d1_1), .out2(is_xor), .out3(is_mulhu), .out4(is_slt), .out5(d1_5), .out6(is_or),
    .out7(is_and), .sel(controlled_buffer_5_out), .en(1'b1));
  assign controlled_buffer_6_out = comparator_5_eq ? Instruction[14:12] : 3'bz;  // Controlled_Buffer controlled_buffer_6
  Decoder #(.select(3)) decoder_2 (
    .out0(is_addi), .out1(is_slli), .out2(is_slti), .out4(is_xori), .out5(d2_5), .out6(is_ori),
    .out7(is_andi), .sel(controlled_buffer_6_out), .en(1'b1));  // open: out3
  Comparator #(.width(7)) comparator_6 (
    .a(controlled_buffer_4_out), .b({7{1'b0}}), .gt(is_srai), .eq(is_srli));  // open: lt
  ROM #(.addrWidth(6), .dataWidth(16)) rom_1 (
    .addr(ROMInput), .data({rom_1_data, WBSel, MemWEn, ALUSel, BSel, ASel, BrUn, ImmSel, RegWEn}));
  Comparator #(.width(7)) comparator_7 (.a(Instruction[6:0]), .b(7'b1100011), .eq(is_branch));  // open: gt, lt
  Priority_Encoder #(.select_enc(6)) priority_encoder_1 (
    .in0(is_add), .in1(is_mul), .in2(is_sub), .in3(is_sll), .in4(is_mulh), .in5(is_mulhu), .in6(is_slt),
    .in7(is_xor), .in8(is_srl), .in9(is_sra), .in10(is_or), .in11(is_and), .in12(is_lb), .in13(is_lh),
    .in14(is_lw), .in15(is_addi), .in16(is_slli), .in17(is_slti), .in18(is_xori), .in19(is_srli),
    .in20(is_srai), .in21(is_ori), .in22(is_andi), .in23(is_sb), .in24(is_sh), .in25(is_sw), .in26(is_beq),
    .in27(is_bne), .in28(is_blt), .in29(is_bge), .in30(is_bltu), .in31(is_bgeu), .in32(is_auipc),
    .in33(is_lui), .in34(is_jal), .in35(is_jalr), .out(ROMInput));  // open: in36, in37, in38, in39, in40, in41, in42, in43, in44, in45, in46, in47, in48, in49, in50, in51, in52, in53, in54, in55, in56, in57, in58, in59, in60, in61, in62, in63, gs, en_out, en_in
  assign controlled_buffer_7_out = is_branch ? Instruction[14:12] : 3'bz;  // Controlled_Buffer controlled_buffer_7
  assign controlled_buffer_8_out = comparator_8_eq ? Instruction[14:12] : 3'bz;  // Controlled_Buffer controlled_buffer_8
  Comparator #(.width(7)) comparator_8 (.a(Instruction[6:0]), .b(7'b0000011), .eq(comparator_8_eq));  // open: gt, lt
  assign controlled_buffer_9_out = comparator_9_eq ? Instruction[14:12] : 3'bz;  // Controlled_Buffer controlled_buffer_9
  Comparator #(.width(7)) comparator_9 (.a(Instruction[6:0]), .b(7'b0100011), .eq(comparator_9_eq));  // open: gt, lt
  Decoder #(.select(3)) decoder_3 (
    .out0(is_beq), .out1(is_bne), .out4(is_blt), .out5(is_bge), .out6(is_bltu), .out7(is_bgeu),
    .sel(controlled_buffer_7_out), .en(1'b1));  // open: out2, out3
  Decoder #(.select(3)) decoder_4 (
    .out0(is_lb), .out1(is_lh), .out2(is_lw), .sel(controlled_buffer_8_out), .en(1'b1));  // open: out3, out4, out5, out6, out7
  Decoder #(.select(3)) decoder_5 (
    .out0(is_sb), .out1(is_sh), .out2(is_sw), .sel(controlled_buffer_9_out), .en(1'b1));  // open: out3, out4, out5, out6, out7
  Comparator #(.width(7)) comparator_10 (.a(Instruction[6:0]), .b(7'b1101111), .eq(is_jal));  // open: gt, lt
  Comparator #(.width(7)) comparator_11 (.a(Instruction[6:0]), .b(7'b1100111), .eq(is_jalr));  // open: gt, lt
  Comparator #(.width(7)) comparator_12 (.a(Instruction[6:0]), .b(7'b0010111), .eq(is_auipc));  // open: gt, lt
  Comparator #(.width(7)) comparator_13 (.a(Instruction[6:0]), .b(7'b0110111), .eq(is_lui));  // open: gt, lt
  assign PCSel = is_branch ? controlled_buffer_12_out : 1'bz;  // Controlled_Buffer controlled_buffer_10
  assign PCSel = not_1_out ? or_1_out : 1'bz;  // Controlled_Buffer controlled_buffer_11
  not not_1 (not_1_out, is_branch);
  or or_1 (or_1_out, is_jal, is_jalr);
  assign controlled_buffer_12_out = is_beq ? BrEq : 1'bz;  // Controlled_Buffer controlled_buffer_12
  assign controlled_buffer_12_out = or_2_out ? BrLt : 1'bz;  // Controlled_Buffer controlled_buffer_13
  or or_2 (or_2_out, is_bge, is_bgeu);
  assign controlled_buffer_12_out = is_bne ? not_2_out : 1'bz;  // Controlled_Buffer controlled_buffer_14
  not not_2 (not_2_out, BrEq);
  assign controlled_buffer_12_out = or_3_out ? BrLt : 1'bz;  // Controlled_Buffer controlled_buffer_15
  or or_3 (or_3_out, is_blt, is_bltu);

  // Other names for the same wires on the sheet: Opcode[6:0] = Instruction[6:0]; rd[4:0] = Instruction[11:7];
  //   funct3[2:0] = Instruction[14:12]; rs1[4:0] = Instruction[19:15]; rs2[4:0] = Instruction[24:20];
  //   funct7[6:0] = Instruction[31:25]

  // Notes on the sheet:
  //   R-type
  //   I-type
  //   Instruction Selection 
  //   INPUTS to your circuit
  //   Connect ROM Input here ->
  //   contents of rom_1 (hex, n*v repeats v):
  //   100b 140b 160b 108b 148b 158b 110b 120b 128b 168b 130b 138b 41 41 41 1041 10c1 1141 1241 12c1 16c1
  //   1341 13c1 3842 3842 3842 4*3064 3074 3074 1067 17c7 2069 2041
  //   ROM FOR CONTROL LOGIC
  //   B-type
  //   I-type Load
  //   S-type Load
  //   DON'T CHANGE THE LOCATIONS OF THE INPUTS AND OUTPUTS!
  //   This is only if you choose to do the ROM option
  //   CONNECT
  //   WIRE
  //   TO
  //   USE
  //   ROM
  //   J-type 
  //   I-type Jump
  //   U-type Jump
  //   U-type Load
  //   OUTPUT from your circuit
  //   Reminder: If using ROM, use combinational logic for PCSel
endmodule
