// Logisim project partial-load.circ as structural Verilog: 1 circuit, main circuit partial_load
module partial_load (
  input  [31:0] Instruction,
  input  [31:0] MemAddress,
  input  [31:0] DataFromMem,
  output [31:0] DataToReg
);

  wire [1:0] bit_extender_1_out, bit_extender_2_out, bit_extender_3_out;
  wire [7:0] multiplexer_1_out;
  wire [15:0] multiplexer_2_out;
  wire [31:0] bit_extender_4_out, bit_extender_5_out, multiplexer_3_out;

  Bit_Extender #(.in_width(32), .out_width(2), .\type ("input")) bit_extender_1 (
    .in(MemAddress), .out(bit_extender_1_out));  // open: extend
  Bit_Extender #(.in_width(32), .out_width(2), .\type ("input")) bit_extender_2 (
    .in(MemAddress), .out(bit_extender_2_out));  // open: extend
  Bit_Extender #(.in_width(32), .out_width(2), .\type ("input")) bit_extender_3 (
    .in(MemAddress), .out(bit_extender_3_out));  // open: extend
  Multiplexer #(.select(2), .width(8)) multiplexer_1 (
    .in0(DataFromMem[7:0]), .in1(DataFromMem[15:8]), .in2(DataFromMem[23:16]), .in3(DataFromMem[31:24]),
    .out(multiplexer_1_out), .sel(bit_extender_1_out));
  Multiplexer #(.select(2), .width(16)) multiplexer_2 (
    .in0(DataFromMem[15:0]), .in1(DataFromMem[23:8]), .in2(DataFromMem[31:16]), .out(multiplexer_2_out),
    .sel(bit_extender_2_out));  // open: in3
  Multiplexer #(.select(2), .width(32)) multiplexer_3 (
    .in0(DataFromMem), .out(multiplexer_3_out), .sel(bit_extender_3_out));  // open: in1, in2, in3
  assign bit_extender_4_out = {{24{multiplexer_1_out[7]}}, multiplexer_1_out};  // Bit_Extender bit_extender_4
  assign bit_extender_5_out = {{16{multiplexer_2_out[15]}}, multiplexer_2_out};  // Bit_Extender bit_extender_5
  Multiplexer #(.select(3), .width(32)) multiplexer_4 (
    .in0(bit_extender_4_out), .in1(bit_extender_5_out), .in2(multiplexer_3_out), .out(DataToReg),
    .sel(Instruction[14:12]));  // open: in3, in4, in5, in6, in7

  // Other names for the same wires on the sheet: funct3[2:0] = Instruction[14:12]

  // Notes on the sheet:
  //   INPUTS to your circuit
  //   loadByte
  //   loadHalf
  //   loadWord
  //   DON'T CHANGE THE LOCATIONS OF THE INPUTS AND OUTPUTS!
  //   OUTPUT from your circuit
endmodule
