// Logisim project partial-store.circ as structural Verilog: 1 circuit, main circuit partial_store
module partial_store (
  input  [31:0] Instruction,
  input  [31:0] MemAddress,
  input  [31:0] DataFromReg,
  input  MemWEn,
  output [3:0] MemWriteMask,
  output [31:0] DataToMem
);

  wire [1:0] btm2bits;
  wire [3:0] maskBytes, maskHalf, multiplexer_2_out;
  wire [4:0] bit_extender_4_out, bit_extender_6_out, multiplier_1_out, multiplier_2_out;
  wire [7:0] bit_extender_1_out;
  wire [15:0] bit_extender_2_out;
  wire [31:0] bit_extender_3_out, bit_extender_5_out, multiplexer_1_out, outputBytes, outputHalf;

  Bit_Extender #(.in_width(32), .out_width(8)) bit_extender_1 (.in(DataFromReg), .out(bit_extender_1_out));
  Bit_Extender #(.in_width(32)) bit_extender_2 (.in(DataFromReg), .out(bit_extender_2_out));
  assign bit_extender_3_out = {{24{1'b0}}, bit_extender_1_out};  // Bit_Extender bit_extender_3
  assign bit_extender_4_out = {{3{1'b0}}, btm2bits};  // Bit_Extender bit_extender_4
  Shifter #(.width(4)) shifter_1 (.in(4'b0001), .\dist (btm2bits), .out(maskBytes));
  assign bit_extender_5_out = {{16{1'b0}}, bit_extender_2_out};  // Bit_Extender bit_extender_5
  assign bit_extender_6_out = {{3{1'b0}}, btm2bits};  // Bit_Extender bit_extender_6
  Shifter #(.width(4)) shifter_2 (.in(4'b0011), .\dist (btm2bits), .out(maskHalf));
  Multiplier #(.width(5)) multiplier_1 (
    .a(5'b01000), .b(bit_extender_4_out), .out(multiplier_1_out));  // open: cin, cout
  Multiplier #(.width(5)) multiplier_2 (
    .a(5'b01000), .b(bit_extender_6_out), .out(multiplier_2_out));  // open: cin, cout
  Shifter #(.width(32)) shifter_3 (.in(bit_extender_3_out), .\dist (multiplier_1_out), .out(outputBytes));
  Shifter #(.width(32)) shifter_4 (.in(bit_extender_5_out), .\dist (multiplier_2_out), .out(outputHalf));
  Bit_Extender #(.in_width(32), .out_width(2)) bit_extender_7 (.in(MemAddress), .out(btm2bits));
  Multiplexer #(.select(3), .width(32)) multiplexer_1 (
    .in0(outputBytes), .in1(outputHalf), .in2(DataFromReg), .out(multiplexer_1_out), .sel(Instruction[14:12]));  // open: in3, in4, in5, in6, in7
  Multiplexer #(.select(3), .width(4)) multiplexer_2 (
    .in0(maskBytes), .in1(maskHalf), .in2(4'b1111), .out(multiplexer_2_out), .sel(Instruction[14:12]));  // open: in3, in4, in5, in6, in7
  Multiplexer #(.width(32)) multiplexer_3 (.in0({32{1'b0}}), .in1(multiplexer_1_out), .out(DataToMem), .sel(MemWEn));
  Multiplexer #(.width(4)) multiplexer_4 (.in0(4'b0000), .in1(multiplexer_2_out), .out(MemWriteMask), .sel(MemWEn));

  // Other names for the same wires on the sheet: funct3[2:0] = Instruction[14:12]; outputWord[31:0] = DataFromReg

  // Notes on the sheet:
  //   storeHalf
  //   storeWord
  //   INPUTS to your circuit
  //   storeBytes
  //   DON'T CHANGE THE LOCATIONS OF THE INPUTS AND OUTPUTS!
  //   OUTPUT from your circuit
endmodule
