// Logisim project regfile.circ as structural Verilog: 1 circuit, main circuit regfile
module regfile (
  input  [4:0] ReadIndex1,
  input  [4:0] ReadIndex2,
  input  [4:0] WriteIndex,
  input  [31:0] WriteData,
  input  RegWEn,
  input  clk,
  output [31:0] ra,
  output [31:0] sp,
  output [31:0] t0,
  output [31:0] t1,
  output [31:0] t2,
  output [31:0] s0,
  output [31:0] s1,
  output [31:0] a0,
  output [31:0] ReadData1,
  output [31:0] ReadData2
);

  wire x0_we, x1_we, x2_we, x3_we, x4_we, x5_we, x6_we, x7_we, x8_we, x9_we, x10_we, x11_we, x12_we, x13_we,
       x14_we, x15_we, x16_we, x17_we, x18_we, x19_we, x20_we, x21_we, x22_we, x23_we, x24_we, x25_we,
       x26_we, x27_we, x28_we, x29_we, x30_we, x31_we;
  wire [31:0] a1, a2, a3, a4, a5, a6, a7, gp, s2, s3, s4, s5, s6, s7, s8, s9, s10, s11, t3, t4, t5, t6, tp,
       x0, xor_1_out;

  Demultiplexer #(.select(5)) demultiplexer_1 (
    .out0(x0_we), .out1(x1_we), .out2(x2_we), .out3(x3_we), .out4(x4_we), .out5(x5_we), .out6(x6_we),
    .out7(x7_we), .out8(x8_we), .out9(x9_we), .out10(x10_we), .out11(x11_we), .out12(x12_we), .out13(x13_we),
    .out14(x14_we), .out15(x15_we), .out16(x16_we), .out17(x17_we), .out18(x18_we), .out19(x19_we),
    .out20(x20_we), .out21(x21_we), .out22(x22_we), .out23(x23_we), .out24(x24_we), .out25(x25_we),
    .out26(x26_we), .out27(x27_we), .out28(x28_we), .out29(x29_we), .out30(x30_we), .out31(x31_we),
    .in(RegWEn), .sel(WriteIndex));
  assign xor_1_out = WriteData ^ WriteData;  // XOR_Gate xor_1, 32 bits wide
  Register #(.width(32)) zero_x0 (.D(xor_1_out), .en(x0_we), .clk(clk), .Q(x0));  // open: clr
  Register #(.width(32)) ra_x1 (.D(WriteData), .en(x1_we), .clk(clk), .Q(ra));  // open: clr
  Register #(.width(32)) sp_x2 (.D(WriteData), .en(x2_we), .clk(clk), .Q(sp));  // open: clr
  Register #(.width(32)) gp_x3 (.D(WriteData), .en(x3_we), .clk(clk), .Q(gp));  // open: clr
  Register #(.width(32)) tp_x4 (.D(WriteData), .en(x4_we), .clk(clk), .Q(tp));  // open: clr
  Register #(.width(32)) t0_temp_reg (.D(WriteData), .en(x5_we), .clk(clk), .Q(t0));  // open: clr
  Register #(.width(32)) t1_temp_reg (.D(WriteData), .en(x6_we), .clk(clk), .Q(t1));  // open: clr
  Register #(.width(32)) t2_temp_reg (.D(WriteData), .en(x7_we), .clk(clk), .Q(t2));  // open: clr
  Register #(.width(32)) s0_saved_reg (.D(WriteData), .en(x8_we), .clk(clk), .Q(s0));  // open: clr
  Register #(.width(32)) s1_saved_reg (.D(WriteData), .en(x9_we), .clk(clk), .Q(s1));  // open: clr
  Register #(.width(32)) a0_arg_reg (.D(WriteData), .en(x10_we), .clk(clk), .Q(a0));  // open: clr
  Register #(.width(32)) a1_arg_reg (.D(WriteData), .en(x11_we), .clk(clk), .Q(a1));  // open: clr
  Register #(.width(32)) a2_arg_reg (.D(WriteData), .en(x12_we), .clk(clk), .Q(a2));  // open: clr
  Register #(.width(32)) a3_arg_reg (.D(WriteData), .en(x13_we), .clk(clk), .Q(a3));  // open: clr
  Register #(.width(32)) a4_arg_reg (.D(WriteData), .en(x14_we), .clk(clk), .Q(a4));  // open: clr
  Register #(.width(32)) a5_arg_reg (.D(WriteData), .en(x15_we), .clk(clk), .Q(a5));  // open: clr
  Register #(.width(32)) a6_reg (.D(WriteData), .en(x16_we), .clk(clk), .Q(a6));  // open: clr
  Register #(.width(32)) a7_reg (.D(WriteData), .en(x17_we), .clk(clk), .Q(a7));  // open: clr
  Register #(.width(32)) s2_reg (.D(WriteData), .en(x18_we), .clk(clk), .Q(s2));  // open: clr
  Register #(.width(32)) s3_reg (.D(WriteData), .en(x19_we), .clk(clk), .Q(s3));  // open: clr
  Register #(.width(32)) s4_reg (.D(WriteData), .en(x20_we), .clk(clk), .Q(s4));  // open: clr
  Register #(.width(32)) s5_reg (.D(WriteData), .en(x21_we), .clk(clk), .Q(s5));  // open: clr
  Register #(.width(32)) s6_reg (.D(WriteData), .en(x22_we), .clk(clk), .Q(s6));  // open: clr
  Register #(.width(32)) s7_reg (.D(WriteData), .en(x23_we), .clk(clk), .Q(s7));  // open: clr
  Register #(.width(32)) s8_reg (.D(WriteData), .en(x24_we), .clk(clk), .Q(s8));  // open: clr
  Register #(.width(32)) s9_reg (.D(WriteData), .en(x25_we), .clk(clk), .Q(s9));  // open: clr
  Register #(.width(32)) s10_reg (.D(WriteData), .en(x26_we), .clk(clk), .Q(s10));  // open: clr
  Register #(.width(32)) s11_reg (.D(WriteData), .en(x27_we), .clk(clk), .Q(s11));  // open: clr
  Register #(.width(32)) t3_reg (.D(WriteData), .en(x28_we), .clk(clk), .Q(t3));  // open: clr
  Register #(.width(32)) t4_Reg (.D(WriteData), .en(x29_we), .clk(clk), .Q(t4));  // open: clr
  Register #(.width(32)) t5_Reg (.D(WriteData), .en(x30_we), .clk(clk), .Q(t5));  // open: clr
  Register #(.width(32)) t6_Reg (.D(WriteData), .en(x31_we), .clk(clk), .Q(t6));  // open: clr
  Multiplexer #(.select(5), .width(32)) multiplexer_1 (
    .in0(x0), .in1(ra), .in2(sp), .in3(gp), .in4(tp), .in5(t0), .in6(t1), .in7(t2), .in8(s0), .in9(s1),
    .in10(a0), .in11(a1), .in12(a2), .in13(a3), .in14(a4), .in15(a5), .in16(a6), .in17(a7), .in18(s2),
    .in19(s3), .in20(s4), .in21(s5), .in22(s6), .in23(s7), .in24(s8), .in25(s9), .in26(s10), .in27(s11),
    .in28(t3), .in29(t4), .in30(t5), .in31(t6), .out(ReadData1), .sel(ReadIndex1));
  Multiplexer #(.select(5), .width(32)) multiplexer_2 (
    .in0(x0), .in1(ra), .in2(sp), .in3(gp), .in4(tp), .in5(t0), .in6(t1), .in7(t2), .in8(s0), .in9(s1),
    .in10(a0), .in11(a1), .in12(a2), .in13(a3), .in14(a4), .in15(a5), .in16(a6), .in17(a7), .in18(s2),
    .in19(s3), .in20(s4), .in21(s5), .in22(s6), .in23(s7), .in24(s8), .in25(s9), .in26(s10), .in27(s11),
    .in28(t3), .in29(t4), .in30(t5), .in31(t6), .out(ReadData2), .sel(ReadIndex2));

  // Notes on the sheet:
  //   INPUTS to your circuit
  //   DON'T CHANGE THE LOCATIONS OF THE INPUTS AND OUTPUTS!
  //   These are DEBUG/TEST outputs from your circuit.
  //   OUTPUTS from your circuit
endmodule
